# Fritzing sketch GPS-turd-power-strip (saved by Fritzing 0.9.3b)
circuit board: 1.30809cm x 2.36502cm
breadboards: 1

parts:
  C1 = Electrolytic Capacitor [capacitance=100µF package="100 mil [THT, electrolytic]"]
  +5V = female pin header, 5 pins [form="♀ (female)"]
  GND = female pin header, 5 pins [form="♀ (female)"]

nets:
  N1: C1.-, +5V.pin1, +5V.pin2, +5V.pin3, +5V.pin4, +5V.pin5
  N2: C1.+, GND.pin1, GND.pin2, GND.pin3, GND.pin4, GND.pin5

notes:
  GPS turd
  Power strip
